# Fritzing sketch Untitled Sketch 2 (saved by Fritzing 0.8.7b)
breadboards: 1

parts:
  S1 = Pushbutton [package="[THT]"]
  S2 = Pushbutton [package="[THT]"]
  S3 = Pushbutton [package="[THT]"]
  MBED1 = mbed
  U1 = Nokia 6100 Color LCD [package=nokia6100_lcd]
  R1 = Resistor [tolerance=±5% resistance=4.7k package=THT]  # not connected
  R2 = Resistor [tolerance=±5% resistance=4.7k package=THT]
  R3 = Resistor [tolerance=±5% resistance=4.7k package=THT]

nets:
  N1: S1.Pin_1, S1.Pin_2, MBED1.pin11, R3.Pin_1
  N2: S1.Pin_3, S1.Pin_4
  N3: S2.Pin_1, S2.Pin_2
  N4: S2.Pin_3, S2.Pin_4, MBED1.pin10, R2.Pin_1
  N5: S3.Pin_1, S3.Pin_2
  N6: S3.Pin_3, S3.Pin_4, MBED1.pin9
  N7: MBED1.Vin, R2.Pin_0, R3.Pin_0
  N8: MBED1.pin21, U1.CS
  N9: MBED1.pin22, U1.SCK
  N10: MBED1.pin23, U1.DIO
  N11: MBED1.pin24, U1.RESET
  N12: MBED1.pin25, U1.VDIGITAL
